// Digital circuit CPU_RISCV.dig as structural Verilog
module CPU_RISCV (
  input  clk,
  input  [31:0] SysInput,
  input  in_3
);

  wire and_1_out, and_2_out, and_3_out, not_1_out, or_1_out, u_ALU_Decoder_branch_cond, u_ALU_Unit_zero_flag,
       u_BubbleUnit_hold_sig, u_MainCtrl_alusrc, u_MainCtrl_branch, u_MainCtrl_jumpreg, u_MainCtrl_memread,
       u_MainCtrl_memtoreg, u_MainCtrl_memwrite, u_MainCtrl_pc_shift_ctrl, u_MainCtrl_regwrite,
       u_PipeReg_EX_MEM_branch, u_PipeReg_EX_MEM_jar, u_PipeReg_EX_MEM_memread, u_PipeReg_EX_MEM_memtoreg,
       u_PipeReg_EX_MEM_memwrite, u_PipeReg_EX_MEM_regwrite, u_PipeReg_EX_MEM_zero_flag,
       u_PipeReg_ID_EX_aluscr, u_PipeReg_ID_EX_branch, u_PipeReg_ID_EX_jumpreg, u_PipeReg_ID_EX_memread,
       u_PipeReg_ID_EX_memtoreg, u_PipeReg_ID_EX_memwrite, u_PipeReg_ID_EX_pc_shift_ctrl,
       u_PipeReg_ID_EX_regwrite, u_PipeReg_MEM_WB_memtoreg, u_PipeReg_MEM_WB_regwrite;
  wire [1:0] u_BypassUnit_fwdmuxa, u_BypassUnit_fwdmuxb, u_MainCtrl_aluop, u_PipeReg_ID_EX_aluop;
  wire [2:0] u_MainCtrl_funct3, u_PipeReg_ID_EX_funct3;
  wire [3:0] u_ALU_Decoder_alu_control;
  wire [4:0] u_FetchStage_rd_addr, u_FetchStage_rs1_addr, u_FetchStage_rs2_addr, u_PipeReg_EX_MEM_rd,
       u_PipeReg_ID_EX_rs1, u_PipeReg_ID_EX_rs2, u_PipeReg_MEM_WB_rd;
  wire [6:0] u_MainCtrl_funct7, u_MainCtrl_opcode, u_PipeReg_ID_EX_funct7, u_PipeReg_ID_EX_opcode;
  wire [15:0] ramdualport_1_d, ramdualport_2_d, u_AddrUnpacker_unpacked_high, u_AddrUnpacker_unpacked_low,
       u_DataUnpacker_unpacked_high, u_DataUnpacker_unpacked_low;
  wire [31:0] GPR_Block_da, GPR_Block_db, multiplexer_1_out, multiplexer_2_out, multiplexer_3_out,
       multiplexer_4_out, multiplexer_5_out, multiplexer_6_out, multiplexer_7_out, u_Adder32_resultsum,
       u_ALU_Unit_alu_out, u_DataPacker_packed_out, u_FetchStage_addr_out, u_FetchStage_fetched_instr,
       u_FetchStage_next_addr_out, u_ImmExtender_extended_imm, u_PipeReg_EX_MEM_alu_out,
       u_PipeReg_EX_MEM_pc2, u_PipeReg_EX_MEM_regdatab, u_PipeReg_ID_EX_imm, u_PipeReg_ID_EX_pc,
       u_PipeReg_ID_EX_regdataa, u_PipeReg_ID_EX_regdatab, u_PipeReg_MEM_WB_alu_out,
       u_PipeReg_MEM_WB_memdata, u_ProgCounter_addr_out;

  Multiplexer #(.Bits(32)) multiplexer_1 (
    .sel(or_1_out), .in_0(u_ProgCounter_addr_out), .in_1(u_PipeReg_EX_MEM_pc2), .out(multiplexer_1_out));
  ProgCounter #(.applicationType("GHDL"), .CodeFile("rtl\\PC.vhd")) u_ProgCounter (
    .clock(clk), .rst_n(in_3), .addr_in(multiplexer_1_out), .w_en(not_1_out),
    .addr_out(u_ProgCounter_addr_out));
  FetchStage #(.applicationType("GHDL"), .CodeFile("rtl\\instr_fetch.vhd")) u_FetchStage (
    .clock(clk), .w_en(not_1_out), .addr_in(u_ProgCounter_addr_out),
    .next_addr_in(u_FetchStage_next_addr_out), .raw_instr(SysInput), .addr_out(u_FetchStage_addr_out),
    .next_addr_out(u_FetchStage_next_addr_out), .fetched_instr(u_FetchStage_fetched_instr),
    .rs1_addr(u_FetchStage_rs1_addr), .rs2_addr(u_FetchStage_rs2_addr), .rd_addr(u_FetchStage_rd_addr));
  BubbleUnit #(.applicationType("GHDL"), .CodeFile("rtl\\Hazard.vhd")) u_BubbleUnit (
    .clock(clk), .MemRead(u_MainCtrl_memtoreg), .rs1_addr(u_FetchStage_rs1_addr),
    .rs2_addr(u_FetchStage_rs2_addr), .rd_addr(u_FetchStage_rd_addr), .hold_sig(u_BubbleUnit_hold_sig));
  not not_1 (not_1_out, u_BubbleUnit_hold_sig);
  MainCtrl #(.applicationType("GHDL"), .CodeFile("rtl\\Control.vhd")) u_MainCtrl (
    .op_code_word(u_FetchStage_fetched_instr), .hold_sig(u_BubbleUnit_hold_sig), .Branch(u_MainCtrl_branch),
    .MemRead(u_MainCtrl_memread), .MemtoReg(u_MainCtrl_memtoreg), .ALUop(u_MainCtrl_aluop),
    .MemWrite(u_MainCtrl_memwrite), .ALUsrc(u_MainCtrl_alusrc), .RegWrite(u_MainCtrl_regwrite),
    .funct7(u_MainCtrl_funct7), .funct3(u_MainCtrl_funct3), .opcode(u_MainCtrl_opcode),
    .PC_shift_ctrl(u_MainCtrl_pc_shift_ctrl), .JumpReg(u_MainCtrl_jumpreg));
  RegisterFile #(.AddrBits(5), .Bits(32)) GPR_Block (
    .Din(u_PipeReg_ID_EX_regdatab), .we(u_PipeReg_MEM_WB_regwrite), .Rw(u_PipeReg_MEM_WB_rd), .C(clk),
    .Ra(u_FetchStage_rs1_addr), .Rb(u_FetchStage_rs2_addr), .Da(GPR_Block_da), .Db(GPR_Block_db));
  ImmExtender #(.applicationType("GHDL"), .CodeFile("rtl\\ImmGen.vhd")) u_ImmExtender (
    .instruction(u_FetchStage_fetched_instr), .extended_imm(u_ImmExtender_extended_imm));
  PipeReg_ID_EX #(.applicationType("GHDL"), .CodeFile("rtl\\idex.vhd")) u_PipeReg_ID_EX (
    .clock(clk), .Branch_in(u_MainCtrl_branch), .MemRead_in(u_MainCtrl_memread),
    .MemtoReg_in(u_MainCtrl_memtoreg), .ALUop_in(u_MainCtrl_aluop), .MemWrite_in(u_MainCtrl_memwrite),
    .ALUscr_in(u_MainCtrl_alusrc), .RegWrite_in(u_MainCtrl_regwrite), .funct7_in(u_MainCtrl_funct7),
    .funct3_in(u_MainCtrl_funct3), .opcode_in(u_MainCtrl_opcode),
    .PC_shift_ctrl_in(u_MainCtrl_pc_shift_ctrl), .JumpReg_in(u_MainCtrl_jumpreg),
    .PC_in(u_FetchStage_addr_out), .RegDataA_in(GPR_Block_da), .RegDataB_in(GPR_Block_db),
    .imm_in(u_ImmExtender_extended_imm), .rs1_in(u_FetchStage_rs1_addr), .rs2_in(u_FetchStage_rs1_addr),
    .rd_in(u_FetchStage_rd_addr), .Branch(u_PipeReg_ID_EX_branch), .MemRead(u_PipeReg_ID_EX_memread),
    .MemtoReg(u_PipeReg_ID_EX_memtoreg), .ALUop(u_PipeReg_ID_EX_aluop), .MemWrite(u_PipeReg_ID_EX_memwrite),
    .ALUscr(u_PipeReg_ID_EX_aluscr), .RegWrite(u_PipeReg_ID_EX_regwrite), .funct7(u_PipeReg_ID_EX_funct7),
    .funct3(u_PipeReg_ID_EX_funct3), .opcode(u_PipeReg_ID_EX_opcode),
    .PC_shift_ctrl(u_PipeReg_ID_EX_pc_shift_ctrl), .JumpReg(u_PipeReg_ID_EX_jumpreg),
    .PC(u_PipeReg_ID_EX_pc), .RegDataA(u_PipeReg_ID_EX_regdataa), .RegDataB(u_PipeReg_ID_EX_regdatab),
    .imm(u_PipeReg_ID_EX_imm), .rs1(u_PipeReg_ID_EX_rs1), .rs2(u_PipeReg_ID_EX_rs2), .rd(u_FetchStage_rd_addr));
  BypassUnit #(.applicationType("GHDL"), .CodeFile("rtl\\Forward.vhd")) u_BypassUnit (
    .clock(clk), .WB_RegWrite(u_PipeReg_MEM_WB_regwrite), .MEM_RegWrite(u_PipeReg_EX_MEM_regwrite),
    .rs1_addr(u_PipeReg_ID_EX_rs1), .rs2_addr(u_PipeReg_ID_EX_rs2), .WB_rd(u_PipeReg_MEM_WB_rd),
    .MEM_rd(u_PipeReg_EX_MEM_rd), .FwdMuxA(u_BypassUnit_fwdmuxa), .FwdMuxB(u_BypassUnit_fwdmuxb));
  ALU_Decoder #(.applicationType("GHDL"), .CodeFile("rtl\\ULA_control.vhd")) u_ALU_Decoder (
    .funct7(u_PipeReg_ID_EX_funct7), .funct3(u_PipeReg_ID_EX_funct3), .opcode(u_PipeReg_ID_EX_opcode),
    .ALUop(u_PipeReg_ID_EX_aluop), .alu_control(u_ALU_Decoder_alu_control),
    .branch_cond(u_ALU_Decoder_branch_cond));
  and and_1 (and_1_out, u_PipeReg_ID_EX_pc_shift_ctrl, ~u_PipeReg_ID_EX_aluscr);  // And
  Multiplexer #(.Bits(32)) multiplexer_2 (
    .sel(u_PipeReg_ID_EX_aluscr), .in_0(u_PipeReg_ID_EX_regdatab), .in_1(u_PipeReg_ID_EX_imm),
    .out(multiplexer_2_out));
  Multiplexer #(.Bits(32)) multiplexer_3 (
    .sel(u_PipeReg_ID_EX_jumpreg), .in_0(u_PipeReg_ID_EX_pc), .in_1(u_PipeReg_ID_EX_regdataa),
    .out(multiplexer_3_out));
  Multiplexer #(.Bits(32)) multiplexer_4 (
    .sel(u_PipeReg_ID_EX_pc_shift_ctrl), .in_0(u_PipeReg_ID_EX_regdataa), .in_1(u_PipeReg_ID_EX_pc),
    .out(multiplexer_4_out));
  Multiplexer #(.Bits(32)) multiplexer_5 (
    .sel(and_1_out), .in_0(multiplexer_2_out), .in_1(32'h1), .out(multiplexer_5_out));
  Adder32 #(.applicationType("GHDL"), .CodeFile("rtl\\adder.vhd")) u_Adder32 (
    .OperandA(multiplexer_3_out), .OperandB(u_PipeReg_ID_EX_imm), .ResultSum(u_Adder32_resultsum));
  Multiplexer #(.Selector_Bits(2), .Bits(32)) multiplexer_6 (
    .sel(u_BypassUnit_fwdmuxb), .in_0(multiplexer_5_out), .in_1(u_PipeReg_ID_EX_regdatab),
    .in_2(u_PipeReg_EX_MEM_alu_out), .in_3(u_PipeReg_ID_EX_regdatab), .out(multiplexer_6_out));
  Multiplexer #(.Selector_Bits(2), .Bits(32)) multiplexer_7 (
    .sel(u_BypassUnit_fwdmuxa), .in_0(multiplexer_4_out), .in_1(u_PipeReg_ID_EX_regdatab),
    .in_2(u_PipeReg_EX_MEM_alu_out), .in_3({32{1'b0}}), .out(multiplexer_7_out));
  ALU_Unit #(.applicationType("GHDL"), .CodeFile("rtl\\ULA.vhd")) u_ALU_Unit (
    .SrcMuxA(multiplexer_7_out), .SrcMuxB(multiplexer_6_out), .alu_control(u_ALU_Decoder_alu_control),
    .alu_out(u_ALU_Unit_alu_out), .zero_flag(u_ALU_Unit_zero_flag));
  and and_2 (and_2_out, u_ALU_Decoder_branch_cond, u_ALU_Unit_zero_flag);
  PipeReg_EX_MEM #(.applicationType("GHDL"), .CodeFile("rtl\\exmem.vhd")) u_PipeReg_EX_MEM (
    .clock(clk), .Branch_in(u_PipeReg_ID_EX_branch), .MemRead_in(u_PipeReg_ID_EX_memread),
    .MemtoReg_in(u_PipeReg_ID_EX_memtoreg), .MemWrite_in(u_PipeReg_ID_EX_memwrite),
    .RegWrite_in(u_PipeReg_ID_EX_regwrite), .PC2_in(u_Adder32_resultsum),
    .RegDataB_in(u_PipeReg_ID_EX_regdatab), .rd_in(u_FetchStage_rd_addr), .zero_flag_in(and_2_out),
    .alu_out_in(u_ALU_Unit_alu_out), .jar_in(and_1_out), .Branch(u_PipeReg_EX_MEM_branch),
    .MemRead(u_PipeReg_EX_MEM_memread), .MemtoReg(u_PipeReg_EX_MEM_memtoreg),
    .MemWrite(u_PipeReg_EX_MEM_memwrite), .RegWrite(u_PipeReg_EX_MEM_regwrite), .PC2(u_PipeReg_EX_MEM_pc2),
    .RegDataB(u_PipeReg_EX_MEM_regdatab), .rd(u_PipeReg_EX_MEM_rd), .zero_flag(u_PipeReg_EX_MEM_zero_flag),
    .alu_out(u_PipeReg_EX_MEM_alu_out), .jar(u_PipeReg_EX_MEM_jar));
  and and_3 (and_3_out, u_PipeReg_EX_MEM_branch, u_PipeReg_EX_MEM_zero_flag);
  or or_1 (or_1_out, and_3_out, u_PipeReg_EX_MEM_jar);
  DataUnpacker #(.applicationType("GHDL"), .CodeFile("rtl\\spliter.vhd")) u_DataUnpacker (
    .packed_32(u_PipeReg_EX_MEM_regdatab), .unpacked_high(u_DataUnpacker_unpacked_high),
    .unpacked_low(u_DataUnpacker_unpacked_low));
  AddrUnpacker #(.applicationType("GHDL"), .CodeFile("rtl\\spliter.vhd")) u_AddrUnpacker (
    .packed_32(u_PipeReg_EX_MEM_alu_out), .unpacked_high(u_AddrUnpacker_unpacked_high),
    .unpacked_low(u_AddrUnpacker_unpacked_low));
  RAMDualPort #(.AddrBits(16), .Bits(16)) ramdualport_1 (
    .A(u_DataUnpacker_unpacked_high), .Din(u_AddrUnpacker_unpacked_high), .str(u_PipeReg_EX_MEM_memwrite),
    .C(clk), .ld(u_PipeReg_EX_MEM_memread), .D(ramdualport_1_d));
  RAMDualPort #(.AddrBits(16), .Bits(16)) ramdualport_2 (
    .A(u_DataUnpacker_unpacked_low), .Din(u_AddrUnpacker_unpacked_low), .str(u_PipeReg_EX_MEM_memwrite),
    .C(clk), .ld(u_PipeReg_EX_MEM_memread), .D(ramdualport_2_d));
  DataPacker #(.applicationType("GHDL"), .CodeFile("rtl\\joiner.vhd")) u_DataPacker (
    .half_high(ramdualport_1_d), .half_low(ramdualport_2_d), .packed_out(u_DataPacker_packed_out));
  PipeReg_MEM_WB #(.applicationType("GHDL"), .CodeFile("rtl\\memwb.vhd")) u_PipeReg_MEM_WB (
    .clock(clk), .RegWrite_in(u_PipeReg_EX_MEM_regwrite), .MemtoReg_in(u_PipeReg_EX_MEM_memtoreg),
    .MemData_in(u_DataPacker_packed_out), .alu_out_in(u_PipeReg_EX_MEM_alu_out), .rd_in(u_PipeReg_EX_MEM_rd),
    .RegWrite(u_PipeReg_MEM_WB_regwrite), .MemtoReg(u_PipeReg_MEM_WB_memtoreg),
    .MemData(u_PipeReg_MEM_WB_memdata), .alu_out(u_PipeReg_MEM_WB_alu_out), .rd(u_PipeReg_MEM_WB_rd));
  Multiplexer #(.Bits(32)) multiplexer_8 (
    .sel(u_PipeReg_MEM_WB_memtoreg), .in_0(u_PipeReg_MEM_WB_alu_out), .in_1(u_PipeReg_MEM_WB_memdata),
    .out(u_PipeReg_ID_EX_regdatab));
  // also tied to GND on the sheet: {u_PipeReg_ID_EX_regdatab[0], u_PipeReg_ID_EX_regdatab[1], u_PipeReg_ID_EX_regdatab[2], u_PipeReg_ID_EX_regdatab[3], u_PipeReg_ID_EX_regdatab[4], u_PipeReg_ID_EX_regdatab[5], u_PipeReg_ID_EX_regdatab[6], u_PipeReg_ID_EX_regdatab[7], u_PipeReg_ID_EX_regdatab[8], u_PipeReg_ID_EX_regdatab[9], u_PipeReg_ID_EX_regdatab[10], u_PipeReg_ID_EX_regdatab[11], u_PipeReg_ID_EX_regdatab[12], u_PipeReg_ID_EX_regdatab[13], u_PipeReg_ID_EX_regdatab[14], u_PipeReg_ID_EX_regdatab[15], u_PipeReg_ID_EX_regdatab[16], u_PipeReg_ID_EX_regdatab[17], u_PipeReg_ID_EX_regdatab[18], u_PipeReg_ID_EX_regdatab[19], u_PipeReg_ID_EX_regdatab[20], u_PipeReg_ID_EX_regdatab[21], u_PipeReg_ID_EX_regdatab[22], u_PipeReg_ID_EX_regdatab[23], u_PipeReg_ID_EX_regdatab[24], u_PipeReg_ID_EX_regdatab[25], u_PipeReg_ID_EX_regdatab[26], u_PipeReg_ID_EX_regdatab[27], u_PipeReg_ID_EX_regdatab[28], u_PipeReg_ID_EX_regdatab[29], u_PipeReg_ID_EX_regdatab[30], u_PipeReg_ID_EX_regdatab[31]}
endmodule
